// Digital circuit CPU.dig as structural Verilog
module CPU (
  input  A,
  input  B,
  input  A_2,
  input  B_2,
  input  Cin,
  input  A0,
  input  A1,
  input  A2,
  input  A3,
  input  B0,
  input  B1,
  input  B2,
  input  B3,
  input  A_3,
  input  B_3,
  input  Cin_2,
  input  A_4,
  input  B_4,
  input  Cin_3,
  input  A_5,
  input  B_5,
  input  Cin_4,
  input  A_6,
  input  B_6,
  input  Cin_5,
  input  A0_2,
  input  A1_2,
  input  A2_2,
  input  A3_2,
  input  A4,
  input  A5,
  input  A6,
  input  A7,
  input  B0_2,
  input  B1_2,
  input  B2_2,
  input  B3_2,
  input  B4,
  input  B5,
  input  B6,
  input  B7,
  input  Cin_6,
  input  A8,
  input  A9,
  input  A10,
  input  A11,
  input  A12,
  input  A13,
  input  A14,
  input  A15,
  input  B8,
  input  B9,
  input  B10,
  input  B11,
  input  B12,
  input  B13,
  input  B14,
  input  B15,
  input  Cin_7,
  input  A0_3,
  input  A1_3,
  input  A2_3,
  input  A3_3,
  input  A4_2,
  input  A5_2,
  input  A6_2,
  input  A7_2,
  input  B0_3,
  input  B1_3,
  input  B2_3,
  input  B3_3,
  input  B4_2,
  input  B5_2,
  input  B6_2,
  input  B7_2,
  input  Sub,
  input  A0_4,
  input  A1_4,
  input  A2_4,
  input  A3_4,
  input  A4_3,
  input  A5_3,
  input  A6_3,
  input  A7_3,
  input  B0_4,
  input  B1_4,
  input  B2_4,
  input  B3_4,
  input  B4_3,
  input  B5_3,
  input  B6_3,
  input  B7_3,
  input  A0_5,
  input  A1_5,
  input  A2_5,
  input  A3_5,
  input  B0_5,
  input  B1_5,
  input  B2_5,
  input  B3_5,
  input  A0_6,
  input  A1_6,
  input  A2_6,
  input  A3_6,
  input  B0_6,
  input  B1_6,
  input  B2_6,
  input  B3_6,
  input  A1_7,
  input  A2_7,
  input  A3_7,
  input  A4_4,
  input  A5_4,
  input  A6_4,
  input  A7_4,
  input  A0_7,
  input  A17,
  input  A18,
  input  A19,
  input  A20,
  input  A21,
  input  A22,
  input  A23,
  input  A16,
  input  A1_8,
  input  A2_8,
  input  A3_8,
  input  A4_5,
  input  A5_5,
  input  A6_5,
  input  A7_5,
  input  A0_8,
  input  A25,
  input  A26,
  input  A27,
  input  A28,
  input  A29,
  input  A30,
  input  A31,
  input  A24,
  input  A0_9,
  input  A1_9,
  input  A2_9,
  input  A3_9,
  input  A4_6,
  input  A5_6,
  input  A6_6,
  input  A7_6,
  input  B0_7,
  input  B1_7,
  input  B2_7,
  input  B3_7,
  input  B4_4,
  input  B5_4,
  input  B6_4,
  input  B7_4,
  input  A32,
  input  A33,
  input  A34,
  input  A35,
  input  A36,
  input  A37,
  input  A38,
  input  A39,
  input  B16,
  input  B17,
  input  B18,
  input  B19,
  input  B20,
  input  B21,
  input  B22,
  input  B23,
  input  A0_10,
  input  A1_10,
  input  A2_10,
  input  A3_10,
  input  A4_7,
  input  A5_7,
  input  A6_7,
  input  A7_7,
  input  B0_8,
  input  B1_8,
  input  B2_8,
  input  B3_8,
  input  B4_5,
  input  B5_5,
  input  B6_5,
  input  B7_5,
  input  A40,
  input  A41,
  input  A42,
  input  A43,
  input  A44,
  input  A45,
  input  A46,
  input  A47,
  input  B24,
  input  B25,
  input  B26,
  input  B27,
  input  B28,
  input  B29,
  input  B30,
  input  B31,
  input  A0_11,
  input  A1_11,
  input  A2_11,
  input  A3_11,
  input  A4_8,
  input  A5_8,
  input  A6_8,
  input  A7_8,
  input  B0_9,
  input  B1_9,
  input  B2_9,
  input  B3_9,
  input  B4_6,
  input  B5_6,
  input  B6_6,
  input  B7_6,
  input  A48,
  input  A49,
  input  A50,
  input  A51,
  input  A52,
  input  A53,
  input  A54,
  input  A55,
  input  B32,
  input  B33,
  input  B34,
  input  B35,
  input  B36,
  input  B37,
  input  B38,
  input  B39,
  input  SEL_0,
  input  SEL_1,
  input  SEL_2,
  input  A0_12,
  input  A1_12,
  input  A2_12,
  input  A3_12,
  input  A4_9,
  input  A5_9,
  input  A6_9,
  input  A7_9,
  input  B0_10,
  input  B1_10,
  input  B2_10,
  input  B3_10,
  input  B4_7,
  input  B5_7,
  input  B6_7,
  input  B7_7,
  input  clk,
  output Soma,
  output Carry,
  output Soma_2,
  output Carry_Out,
  output S0,
  output S1,
  output S2,
  output S3,
  output OVERFLOW,
  output S0_2,
  output S1_2,
  output S2_2,
  output S3_2,
  output S4,
  output S5,
  output S6,
  output S7,
  output Cout,
  output out_78,
  output out_95,
  output Cout_2,
  output MULT_BIT0,
  output MULT_BIT1,
  output MULT_BIT2,
  output MULT_BIT3,
  output MULT_BIT4,
  output MULT_BIT5,
  output MULT_BIT6,
  output MULT_BIT7,
  output [7:0] Multiplicador,
  output SR_BIT0,
  output SR_BIT1,
  output SR_BIT2,
  output SR_BIT3,
  output SR_BIT4,
  output SR_BIT5,
  output SR_BIT6,
  output SR_BIT7,
  output [7:0] SR,
  output SL_BIT0,
  output SL_BIT1,
  output SL_BIT2,
  output SL_BIT3,
  output SL_BIT4,
  output SL_BIT5,
  output SL_BIT6,
  output SL_BIT7,
  output [7:0] SL,
  output AND_BIT0,
  output AND_BIT1,
  output AND_BIT2,
  output AND_BIT3,
  output AND_BIT4,
  output AND_BIT5,
  output AND_BIT6,
  output AND_BIT7,
  output [7:0] AND,
  output OR_BIT0,
  output OR_BIT1,
  output OR_BIT2,
  output OR_BIT3,
  output OR_BIT4,
  output OR_BIT5,
  output OR_BIT6,
  output OR_BIT7,
  output [7:0] OR,
  output XOR_BIT0,
  output XOR_BIT1,
  output XOR_BIT2,
  output XOR_BIT3,
  output XOR_BIT4,
  output XOR_BIT5,
  output XOR_BIT6,
  output XOR_BIT7,
  output [7:0] XOR,
  output Overflow_2,
  output Overflow_3
);

  wire and_2_out, and_3_out, and_4_out, and_5_out, and_6_out, and_7_out, and_8_out, and_9_out, and_10_out,
       and_11_out, and_12_out, and_13_out, and_15_out, and_16_out, and_17_out, and_18_out, and_19_out,
       and_20_out, and_21_out, and_22_out, and_23_out, and_24_out, and_25_out, and_26_out, and_27_out,
       calculadora_4_bits_1_p14, counter_1_ovf, Cout_Multiplicador, Cout_SL, Cout_Somador, Cout_Subtrator,
       full_adder_1_p4, full_adder_1_p5, full_adder_2_p4, full_adder_2_p5, full_adder_3_p4, full_adder_3_p5,
       full_adder_4_p4, full_adder_4_p5, full_adder_5_p4, full_adder_5_p5, full_adder_6_p4, full_adder_6_p5,
       full_adder_7_p5, half_adder_1_p4, half_adder_2_p4, half_adder_3_p4, half_adder_4_p4,
       multiplexer_2_out, or_2_out, or_3_out, or_4_out, RESET_out, ula_1_overflow, xor_2_out, xor_4_out,
       xor_6_out, xor_8_out, xor_10_out, xor_12_out, xor_13_out, xor_14_out, xor_15_out, xor_16_out,
       xor_17_out, xor_18_out, xor_19_out;
  wire [1:0] counter_1_out;
  wire [7:0] And_t, calculadora_8_bit_2_p18, calculadora_8_bit_3_p18, multiplexer_1_out, Multiplicador_t,
       Or_t, register_1_q, SL_t, Somador, SR_t, Subtrator, subtrator_8_bits_2_p17, ula_1_s_ula, Xor_t;
  wire [10:0] rom_1_d;

  // calculadora_8_bit calculadora_8_bit_1: pin names not known; wires that end beside it: 1'b0, A0_12, A1_12, A2_12, A3_12, A4_9, A5_9, A6_9, A7_9, B0_10, B1_10, B2_10, B3_10, B4_7, B5_7, B6_7, B7_7, Somador, Cout_Somador
  xor xor_1 (Soma, A, B);
  and and_1 (Carry, A, B);
  // subtrator_8_bits subtrator_8_bits_1: pin names not known; wires that end beside it: A0_12, A1_12, A2_12, A3_12, A4_9, A5_9, A6_9, A7_9, B0_10, B1_10, B2_10, B3_10, B4_7, B5_7, B6_7, B7_7, Subtrator, Cout_Subtrator
  xor xor_2 (xor_2_out, A_2, B_2);
  and and_2 (and_2_out, A_2, B_2);
  xor xor_3 (Soma_2, xor_2_out, Cin);
  and and_3 (and_3_out, xor_2_out, Cin);
  or or_1 (Carry_Out, and_2_out, and_3_out);
  // multiplicador multiplicador_1: pin names not known; wires that end beside it: A0_12, A1_12, A2_12, A3_12, B0_10, B1_10, B2_10, B3_10, Multiplicador_t, Cout_Multiplicador
  // shift_right shift_right_1: pin names not known; wires that end beside it: A0_12, A1_12, A2_12, A3_12, A4_9, A5_9, A6_9, A7_9, SR_t
  xor xor_4 (xor_4_out, A0, B0);
  and and_4 (and_4_out, A0, B0);
  xor xor_5 (S0, xor_4_out, 1'b0);
  and and_5 (and_5_out, xor_4_out, 1'b0);
  or or_2 (or_2_out, and_4_out, and_5_out);
  // shift_left shift_left_1: pin names not known; wires that end beside it: A0_12, A1_12, A2_12, A3_12, A4_9, A5_9, A6_9, A7_9, SL_t, Cout_SL
  xor xor_6 (xor_6_out, A1, B1);
  and and_6 (and_6_out, A1, B1);
  xor xor_7 (S1, xor_6_out, or_2_out);
  and and_7 (and_7_out, xor_6_out, or_2_out);
  or or_3 (or_3_out, and_6_out, and_7_out);
  // operacao_and operacao_and_1: pin names not known; wires that end beside it: A0_12, A1_12, A2_12, A3_12, A4_9, A5_9, A6_9, A7_9, B0_10, B1_10, B2_10, B3_10, B4_7, B5_7, B6_7, B7_7, And_t
  xor xor_8 (xor_8_out, A2, B2);
  and and_8 (and_8_out, A2, B2);
  xor xor_9 (S2, xor_8_out, or_3_out);
  and and_9 (and_9_out, xor_8_out, or_3_out);
  or or_4 (or_4_out, and_8_out, and_9_out);
  xor xor_10 (xor_10_out, A3, B3);
  and and_10 (and_10_out, A3, B3);
  // operacao_or operacao_or_1: pin names not known; wires that end beside it: A0_12, A1_12, A2_12, A3_12, A4_9, A5_9, A6_9, A7_9, B0_10, B1_10, B2_10, B3_10, B4_7, B5_7, B6_7, B7_7, Or_t
  xor xor_11 (S3, xor_10_out, or_4_out);
  and and_11 (and_11_out, xor_10_out, or_4_out);
  or or_5 (OVERFLOW, and_10_out, and_11_out);
  Seven_Seg_Hex seven_seg_hex_1 (.d({S3, S0, S2, S1}), .dp(1'b0));
  // operacao_xor operacao_xor_1: pin names not known; wires that end beside it: A0_12, A1_12, A2_12, A3_12, A4_9, A5_9, A6_9, A7_9, B0_10, B1_10, B2_10, B3_10, B4_7, B5_7, B6_7, B7_7, Xor_t
  // calculadora_4_bits calculadora_4_bits_1: pin names not known; wires that end beside it: Cin_6, A0_2, A1_2, A2_2, A3_2, B0_2, B1_2, B2_2, B3_2, S0_2, S1_2, S2_2, S3_2, calculadora_4_bits_1_p14
  // calculadora_4_bits calculadora_4_bits_2: pin names not known; wires that end beside it: calculadora_4_bits_1_p14, A4, A5, A6, A7, B4, B5, B6, B7, S4, S5, S6, S7, Cout
  Multiplexer #(.Selector_Bits(3), .Bits(8)) multiplexer_1 (
    .sel({SEL_2, SEL_1, SEL_0}), .in_0(Somador), .in_1(Subtrator), .in_2(Multiplicador_t), .in_3(SR_t),
    .in_4(SL_t), .in_5(And_t), .in_6(Or_t), .in_7(Xor_t), .out(multiplexer_1_out));
  Seven_Seg_Hex seven_seg_hex_2 (.d(multiplexer_1_out[7:4]), .dp(1'b0));
  Seven_Seg_Hex seven_seg_hex_3 (.d(multiplexer_1_out[3:0]), .dp(1'b0));
  Multiplexer #(.Selector_Bits(3)) multiplexer_2 (
    .sel({SEL_2, SEL_1, SEL_0}), .in_0(Cout_Somador), .in_1(Cout_Subtrator), .in_2(Cout_Multiplicador),
    .in_3(1'b0), .in_4(Cout_SL), .in_5(1'b0), .in_6(1'b0), .in_7(1'b0), .out(multiplexer_2_out));
  LED led_1 (.in(multiplexer_2_out));
  // calculadora_8_bit calculadora_8_bit_2: pin names not known; wires that end beside it: Cin_7, A8, A9, A10, A11, A12, A13, A14, A15, B8, B9, B10, B11, B12, B13, B14, B15, calculadora_8_bit_2_p18, out_78
  Seven_Seg_Hex seven_seg_hex_4 (.d(calculadora_8_bit_2_p18[7:4]), .dp(1'b0));
  Seven_Seg_Hex seven_seg_hex_5 (.d(calculadora_8_bit_2_p18[3:0]), .dp(1'b0));
  Register #(.Bits(8)) register_1 (.D(ula_1_s_ula), .C(clk), .en(1'b1), .Q(register_1_q));
  Button RESET (.out(RESET_out));
  Counter #(.Bits(2)) counter_1 (.en(1'b1), .C(clk), .clr(RESET_out), .out(counter_1_out), .ovf(counter_1_ovf));
  LED led_2 (.in(counter_1_ovf));
  Seven_Seg_Hex seven_seg_hex_6 (.d(register_1_q[7:4]), .dp(1'b0));
  ROM #(.Bits(11)) rom_1 (.A(counter_1_out), .sel(1'b1), .D(rom_1_d));
  Seven_Seg_Hex seven_seg_hex_7 (.d(register_1_q[3:0]), .dp(1'b0));
  ULA ula_1 (
    .A_ULA(register_1_q), .B_ULA(rom_1_d[10:3]), .SEL_0(rom_1_d[0]), .SEL_1(rom_1_d[1]), .SEL_2(rom_1_d[2]),
    .S_ULA(ula_1_s_ula), .Overflow(ula_1_overflow));
  LED led_3 (.in(ula_1_overflow));
  xor xor_12 (xor_12_out, B0_3, Sub);
  xor xor_13 (xor_13_out, B1_3, Sub);
  xor xor_14 (xor_14_out, B2_3, Sub);
  xor xor_15 (xor_15_out, B3_3, Sub);
  xor xor_16 (xor_16_out, B4_2, Sub);
  xor xor_17 (xor_17_out, B5_2, Sub);
  xor xor_18 (xor_18_out, B6_2, Sub);
  xor xor_19 (xor_19_out, B7_2, Sub);
  // calculadora_8_bit calculadora_8_bit_3: pin names not known; wires that end beside it: Sub, A0_3, A1_3, A2_3, A3_3, A4_2, A5_2, A6_2, A7_2, xor_12_out, xor_13_out, xor_14_out, xor_15_out, xor_16_out, xor_17_out, xor_18_out, xor_19_out, calculadora_8_bit_3_p18, out_95
  Seven_Seg_Hex seven_seg_hex_8 (.d(calculadora_8_bit_3_p18[7:4]), .dp(1'b0));
  Seven_Seg_Hex seven_seg_hex_9 (.d(calculadora_8_bit_3_p18[3:0]), .dp(1'b0));
  // subtrator_8_bits subtrator_8_bits_2: pin names not known; wires that end beside it: A0_4, A1_4, A2_4, A3_4, A4_3, A5_3, A6_3, A7_3, B0_4, B1_4, B2_4, B3_4, B4_3, B5_3, B6_3, B7_3, subtrator_8_bits_2_p17, Cout_2
  Seven_Seg_Hex seven_seg_hex_10 (.d(subtrator_8_bits_2_p17[7:4]), .dp(1'b0));
  Seven_Seg_Hex seven_seg_hex_11 (.d(subtrator_8_bits_2_p17[3:0]), .dp(1'b0));
  and and_12 (and_12_out, A0_5, B2_5);
  and and_13 (and_13_out, A0_5, B3_5);
  and and_14 (MULT_BIT0, A0_5, B0_5);
  and and_15 (and_15_out, A0_5, B1_5);
  and and_16 (and_16_out, A1_5, B1_5);
  and and_17 (and_17_out, A1_5, B2_5);
  and and_18 (and_18_out, A1_5, B3_5);
  and and_19 (and_19_out, A1_5, B0_5);
  and and_20 (and_20_out, A2_5, B2_5);
  and and_21 (and_21_out, A2_5, B3_5);
  and and_22 (and_22_out, A2_5, B0_5);
  and and_23 (and_23_out, A2_5, B1_5);
  and and_24 (and_24_out, A3_5, B1_5);
  and and_25 (and_25_out, A3_5, B2_5);
  and and_26 (and_26_out, A3_5, B3_5);
  and and_27 (and_27_out, A3_5, B0_5);
  // half_adder half_adder_1: pin names not known; wires that end beside it: and_19_out, and_15_out, MULT_BIT1, half_adder_1_p4
  // full_adder full_adder_1: pin names not known; wires that end beside it: half_adder_1_p4, and_22_out, and_16_out, full_adder_1_p4, full_adder_1_p5
  // half_adder half_adder_2: pin names not known; wires that end beside it: full_adder_1_p4, and_12_out, MULT_BIT2, half_adder_2_p4
  // full_adder full_adder_2: pin names not known; wires that end beside it: full_adder_1_p5, and_27_out, and_23_out, full_adder_2_p4, full_adder_2_p5
  // full_adder full_adder_3: pin names not known; wires that end beside it: half_adder_2_p4, full_adder_2_p4, and_17_out, full_adder_3_p4, full_adder_3_p5
  // half_adder half_adder_3: pin names not known; wires that end beside it: full_adder_3_p4, and_13_out, MULT_BIT3, half_adder_3_p4
  // full_adder full_adder_4: pin names not known; wires that end beside it: full_adder_2_p5, and_24_out, and_20_out, full_adder_4_p4, full_adder_4_p5
  // full_adder full_adder_5: pin names not known; wires that end beside it: full_adder_3_p5, full_adder_4_p4, and_18_out, full_adder_5_p4, full_adder_5_p5
  // full_adder full_adder_6: pin names not known; wires that end beside it: full_adder_4_p5, and_25_out, and_21_out, full_adder_6_p4, full_adder_6_p5
  // half_adder half_adder_4: pin names not known; wires that end beside it: full_adder_5_p4, half_adder_3_p4, MULT_BIT4, half_adder_4_p4
  // full_adder full_adder_7: pin names not known; wires that end beside it: half_adder_4_p4, full_adder_6_p4, full_adder_5_p5, MULT_BIT5, full_adder_7_p5
  // full_adder full_adder_8: pin names not known; wires that end beside it: full_adder_7_p5, and_26_out, full_adder_6_p5, MULT_BIT6, MULT_BIT7
  // multiplicador multiplicador_2: pin names not known; wires that end beside it: A0_6, A1_6, A2_6, A3_6, B0_6, B1_6, B2_6, B3_6, Multiplicador, Overflow_2
  // shift_right shift_right_2: pin names not known; wires that end beside it: A16, A17, A18, A19, A20, A21, A22, A23, SR
  // shift_left shift_left_2: pin names not known; wires that end beside it: A24, A25, A26, A27, A28, A29, A30, A31, SL, Overflow_3
  xor xor_20 (XOR_BIT0, A0_11, B0_9);
  xor xor_21 (XOR_BIT1, A1_11, B1_9);
  xor xor_22 (XOR_BIT2, A2_11, B2_9);
  xor xor_23 (XOR_BIT3, A3_11, B3_9);
  xor xor_24 (XOR_BIT4, A4_8, B4_6);
  xor xor_25 (XOR_BIT5, A5_8, B5_6);
  xor xor_26 (XOR_BIT6, A6_8, B6_6);
  xor xor_27 (XOR_BIT7, A7_8, B7_6);
  and and_28 (AND_BIT0, A0_9, B0_7);
  and and_29 (AND_BIT1, A1_9, B1_7);
  and and_30 (AND_BIT2, A2_9, B2_7);
  and and_31 (AND_BIT3, A3_9, B3_7);
  and and_32 (AND_BIT4, A4_6, B4_4);
  and and_33 (AND_BIT5, A5_6, B5_4);
  and and_34 (AND_BIT6, A6_6, B6_4);
  and and_35 (AND_BIT7, A7_6, B7_4);
  or or_6 (OR_BIT0, A0_10, B0_8);
  or or_7 (OR_BIT1, A1_10, B1_8);
  or or_8 (OR_BIT2, A2_10, B2_8);
  or or_9 (OR_BIT3, A3_10, B3_8);
  or or_10 (OR_BIT4, A4_7, B4_5);
  or or_11 (OR_BIT5, A5_7, B5_5);
  or or_12 (OR_BIT6, A6_7, B6_5);
  or or_13 (OR_BIT7, A7_7, B7_5);
  // operacao_and operacao_and_2: pin names not known; wires that end beside it: A32, A33, A34, A35, A36, A37, A38, A39, B16, B17, B18, B19, B20, B21, B22, B23, AND
  // operacao_or operacao_or_2: pin names not known; wires that end beside it: A40, A41, A42, A43, A44, A45, A46, A47, B24, B25, B26, B27, B28, B29, B30, B31, OR
  // operacao_xor operacao_xor_2: pin names not known; wires that end beside it: A48, A49, A50, A51, A52, A53, A54, A55, B32, B33, B34, B35, B36, B37, B38, B39, XOR

  assign SL_BIT0 = 1'b0;
  assign SL_BIT1 = A0_8;
  assign SL_BIT2 = A1_8;
  assign SL_BIT3 = A2_8;
  assign SL_BIT4 = A3_8;
  assign SL_BIT5 = A4_5;
  assign SL_BIT6 = A5_5;
  assign SL_BIT7 = A6_5;
  assign SR_BIT0 = A1_7;
  assign SR_BIT1 = A2_7;
  assign SR_BIT2 = A3_7;
  assign SR_BIT3 = A4_4;
  assign SR_BIT4 = A5_4;
  assign SR_BIT5 = A6_4;
  assign SR_BIT6 = A7_4;
  assign SR_BIT7 = 1'b0;

  // Other names for the same wires on the sheet: A0_MULTI = A0_5; A0_t = A0_12; A1_MULTI = A1_5; A1_t = A1_12;
  //   A2_MULTI = A2_5; A2_t = A2_12; A3_MULTI = A3_5; A3_t = A3_12; A4_t = A4_9; A5_t = A5_9; A6_t = A6_9;
  //   A7_t = A7_9; B0_MULTI = B0_5; B0_t = B0_10; B1_MULTI = B1_5; B1_t = B1_10; B2_MULTI = B2_5; B2_t = B2_10;
  //   B3_MULTI = B3_5; B3_t = B3_10; B4_t = B4_7; B5_t = B5_7; B6_t = B6_7; B7_t = B7_7;
  //   Seleção[2:0] = {SEL_2, SEL_1, SEL_0}

  // Notes on the sheet:
  //   somador de 8 bits
  //   Somador de 1/2 bit
  //   Meio Somador (Half Adder)
  //   Subtrator de 8 bits
  //   Somador Completo (Full Adder)
  //   Somador de 1 bit
  //   MULTIPLICADOR DE 8 BITS
  //   SHIFT RIGHT
  //   Full Adder 0
  //   SHIFT LEFT
  //   Full Adder 1
  //   Somador de 4 bits
  //   OPERAÇÃO AND
  //   Full Adder 2
  //   Full Adder 3
  //   OPERAÇÃO OR
  //   OPERAÇÃO XOR
  //   2 somadores de 4 bits
  //   ALU
  //   Overflow
  //   ATIVAÇÃO DO ALU
  //   000: Somador
  //   001: Subtrator
  //   010: Multiplicador
  //   011: SR
  //   100: SL
  //   101: And
  //   110: Or
  //   111: Xor
  //   CPU
  //   contents of rom_1 (hex, n*v repeats v):
  //   50,12,c,7d
  //   A0·B1
  //   A0·B2
  //   A0·B3
  //   A0·B0
  //   A1·B2
  //   A1·B3
  //   A1·B1
  //   A1·B0
  //   A2·B1
  //   A2·B2
  //   A2·B3
  //   A2·B0
  //   A3·B2
  //   A3·B3
  //   A3·B0
  //   A3·B1
  //   ESQUERDA = MULTIPLICAR POR 2
  //   DIREITA = DIVIDIR POR 2
endmodule
