// Digital circuit ULA.dig as structural Verilog
module ULA (
  input  [7:0] A_ULA,
  input  [7:0] B_ULA,
  input  SEL_0,
  input  SEL_1,
  input  SEL_2,
  output [7:0] S_ULA,
  output Overflow
);

  wire Cout_Multiplicador, Cout_SL, Cout_Somador, Cout_Subtrator;
  wire [7:0] And, Multiplicador, Or, SL, Somador, SR, Subtrator, Xor;

  // calculadora_8_bit calculadora_8_bit_1: pin names not known; wires that end beside it: 1'b0, A_ULA[0], A_ULA[1], A_ULA[2], A_ULA[3], A_ULA[4], A_ULA[5], A_ULA[6], A_ULA[7], B_ULA[0], B_ULA[1], B_ULA[2], B_ULA[3], B_ULA[4], B_ULA[5], B_ULA[6], B_ULA[7], Somador, Cout_Somador
  // subtrator_8_bits subtrator_8_bits_1: pin names not known; wires that end beside it: A_ULA[0], A_ULA[1], A_ULA[2], A_ULA[3], A_ULA[4], A_ULA[5], A_ULA[6], A_ULA[7], B_ULA[0], B_ULA[1], B_ULA[2], B_ULA[3], B_ULA[4], B_ULA[5], B_ULA[6], B_ULA[7], Subtrator, Cout_Subtrator
  // multiplicador multiplicador_1: pin names not known; wires that end beside it: A_ULA[0], A_ULA[1], A_ULA[2], A_ULA[3], B_ULA[0], B_ULA[1], B_ULA[2], B_ULA[3], Multiplicador, Cout_Multiplicador
  // shift_right shift_right_1: pin names not known; wires that end beside it: A_ULA[0], A_ULA[1], A_ULA[2], A_ULA[3], A_ULA[4], A_ULA[5], A_ULA[6], A_ULA[7], SR
  // shift_left shift_left_1: pin names not known; wires that end beside it: A_ULA[0], A_ULA[1], A_ULA[2], A_ULA[3], A_ULA[4], A_ULA[5], A_ULA[6], A_ULA[7], SL, Cout_SL
  // operacao_and operacao_and_1: pin names not known; wires that end beside it: A_ULA[0], A_ULA[1], A_ULA[2], A_ULA[3], A_ULA[4], A_ULA[5], A_ULA[6], A_ULA[7], B_ULA[0], B_ULA[1], B_ULA[2], B_ULA[3], B_ULA[4], B_ULA[5], B_ULA[6], B_ULA[7], And
  // operacao_or operacao_or_1: pin names not known; wires that end beside it: A_ULA[0], A_ULA[1], A_ULA[2], A_ULA[3], A_ULA[4], A_ULA[5], A_ULA[6], A_ULA[7], B_ULA[0], B_ULA[1], B_ULA[2], B_ULA[3], B_ULA[4], B_ULA[5], B_ULA[6], B_ULA[7], Or
  // operacao_xor operacao_xor_1: pin names not known; wires that end beside it: A_ULA[0], A_ULA[1], A_ULA[2], A_ULA[3], A_ULA[4], A_ULA[5], A_ULA[6], A_ULA[7], B_ULA[0], B_ULA[1], B_ULA[2], B_ULA[3], B_ULA[4], B_ULA[5], B_ULA[6], B_ULA[7], Xor
  Multiplexer #(.Selector_Bits(3), .Bits(8)) multiplexer_1 (
    .sel({SEL_2, SEL_1, SEL_0}), .in_0(Somador), .in_1(Subtrator), .in_2(Multiplicador), .in_3(SR),
    .in_4(SL), .in_5(And), .in_6(Or), .in_7(Xor), .out(S_ULA));
  Multiplexer #(.Selector_Bits(3)) multiplexer_2 (
    .sel({SEL_2, SEL_1, SEL_0}), .in_0(Cout_Somador), .in_1(Cout_Subtrator), .in_2(Cout_Multiplicador),
    .in_3(1'b0), .in_4(Cout_SL), .in_5(1'b0), .in_6(1'b0), .in_7(1'b0), .out(Overflow));

  // Other names for the same wires on the sheet: A0 = A_ULA[0]; A1 = A_ULA[1]; A2 = A_ULA[2]; A3 = A_ULA[3];
  //   A4 = A_ULA[4]; A5 = A_ULA[5]; A6 = A_ULA[6]; A7 = A_ULA[7]; B0 = B_ULA[0]; B1 = B_ULA[1]; B2 = B_ULA[2];
  //   B3 = B_ULA[3]; B4 = B_ULA[4]; B5 = B_ULA[5]; B6 = B_ULA[6]; B7 = B_ULA[7]; Seleção[2:0] = {SEL_2, SEL_1, SEL_0}

  // Notes on the sheet:
  //   somador de 8 bits
  //   Subtrator de 8 bits
  //   MULTIPLICADOR DE 8 BITS
  //   SHIFT RIGHT
  //   SHIFT LEFT
  //   OPERAÇÃO AND
  //   OPERAÇÃO OR
  //   OPERAÇÃO XOR
  //   ALU
  //   Overflow
  //   ATIVAÇÃO DO ALU
  //   000: Somador
  //   001: Subtrator
  //   010: Multiplicador
  //   011: SR
  //   100: SL
  //   101: And
  //   110: Or
  //   111: Xor
endmodule
